# Fritzing sketch Schematic (saved by Fritzing 0.9.3b)
breadboards: 1

parts:
  Part1 = Arduino Uno (Rev3)
  Raspberry_Pi1 = Raspberry Pi 2
  Part4 = Logic Level Converter
  Part2 = Ambient Light Sensor (TEMT6000 Breakout Board)

nets:
  N1: Part1.A0, Part2.S
  GND: Part1.GND, Raspberry_Pi1.GND, Part4.GND, Part2.GND
  N2: Part1.D0/RX, Part4.RX_HV
  N3: Part1.D1/TX, Part4.TX_HV
  5V: Part1.5V, Part4.HV, Part2.VCC
  N4: Raspberry_Pi1.GPIO3, Part4.LV
  N5: Raspberry_Pi1.GPIO15, Part4.RX_LV
  N6: Raspberry_Pi1.GPIO14, Part4.TX_LV
